# Fritzing sketch memory (saved by Fritzing 0.9.2b)
breadboards: 1

parts:
  R1 = Resistor [tolerance=±5% resistance=220 package=THT]
  R2 = Resistor [tolerance=±5% resistance=220 package=THT]
  R3 = Resistor [tolerance=±5% resistance=220 package=THT]
  S1 = Pushbutton [package="[THT]"]
  R4 = Resistor [tolerance=±5% resistance=220 package=THT]
  R5 = Resistor [tolerance=±5% resistance=220 package=THT]
  R6 = Resistor [tolerance=±5% resistance=220 package=THT]
  R7 = Resistor [tolerance=±5% resistance=220 package=THT]
  R8 = Resistor [tolerance=±5% resistance=220 package=THT]
  LED1 = LED - 5mm [color="Yellow (592nm)" package="5 mm [THT]"]
  LED2 = LED - 5mm [color="Green (555nm)" package="5 mm [THT]"]
  LED3 = LED - 5mm [color="Red (633nm)" package="5 mm [THT]"]
  S2 = Pushbutton [package="[THT]"]
  S3 = Pushbutton [package="[THT]"]
  S4 = Pushbutton [package="[THT]"]
  J1 = Piezo Speaker
  LED4 = LED - 5mm [color="Blue (470nm)" package="5 mm [THT]"]
  Bauteil1 = Arduino Mega Proto Shield (v6) [part_number=2560]
  VCC1 = Battery

nets:
  N1: R1.Pin_0, S1.Pin_3, S1.Pin_4, Bauteil1.D10
  N2: R1.Pin_1, R2.Pin_1, R3.Pin_1, R4.Pin_1, R5.Pin_1, R6.Pin_1, R7.Pin_1, R8.Pin_1, J1.pin1, Bauteil1.GND, VCC1.-
  N3: R2.Pin_0, LED4.cathode
  N4: R3.Pin_0, S2.Pin_3, S2.Pin_4, Bauteil1.D8
  N5: S1.Pin_1, S1.Pin_2, S2.Pin_1, S2.Pin_2, S3.Pin_1, S3.Pin_2, S4.Pin_1, S4.Pin_2, Bauteil1.+3V3, VCC1.+
  N6: R4.Pin_0, LED1.cathode
  N7: R5.Pin_0, S3.Pin_3, S3.Pin_4, Bauteil1.D5
  N8: R6.Pin_0, S4.Pin_3, S4.Pin_4, Bauteil1.D3
  N9: R7.Pin_0, LED2.cathode
  N10: R8.Pin_0, LED3.cathode
  N11: LED1.anode, Bauteil1.D6
  N12: LED2.anode, Bauteil1.D4
  N13: LED3.anode, Bauteil1.D2
  N14: LED4.anode, Bauteil1.D9

// code stored in the sketch: memory.ino
// Variablen deffinition LED 4 Farben + Taster 4x
int LEDblue= 9;
int LEDred=2;
int LEDgreen=4;
int LEDyellow=6;
int Tblue=10;
int Tred=3;
int Tgreen=5;
int Tyellow=8;
int Ton = 1;
int TonHigh=0;
void setup() {
  // put your setup code here, to run once:
  pinMode(LEDblue,OUTPUT);
  pinMode(LEDred, OUTPUT);
  pinMode(LEDgreen, OUTPUT);
  pinMode(LEDyellow, OUTPUT);
  pinMode(Tblue,INPUT);
  pinMode(Tred,INPUT);
  pinMode(Tgreen,INPUT);
  pinMode(Tyellow,INPUT);
  pinMode(Ton, OUTPUT);

}

void loop() {
  // put your main code here, to run repeatedly:
testTaster();
    
}
void testTaster(){
    if(digitalRead(Tblue) == HIGH){
      TonHigh = 2093;
      LED(LEDblue);
    }
    else if (digitalRead(Tred)==HIGH){
      TonHigh = 175;
      LED(LEDred);
      }
      else if(digitalRead(Tgreen)==HIGH){
        TonHigh = 4978;
          LED(LEDgreen);
        }
        else if(digitalRead(Tyellow)==HIGH){
          TonHigh = 3520;
          LED(LEDyellow);

          }
  }

void LED(int LedId){
  digitalWrite(LedId,HIGH);
  tone(Ton,TonHigh);
  delay(500);
  noTone(Ton);
  delay(2000);
  digitalWrite(LedId,LOW);
  }
